# Fritzing sketch PhotocellTimer (saved by Fritzing 0.9.3b)
breadboards: 1

parts:
  R1 = Photocell (LDR) [package=THT]
  R2 = Photocell (LDR) [package=THT]
  R3 = Resistor [tolerance=±5% resistance=220 package=THT]
  R4 = Resistor [tolerance=±5% resistance=220 package=THT]
  S1 = Pushbutton [package="[THT]"]
  Part1 = Arduino Pro Mini v13

nets (from the breadboard view):
  N1: R1.pin_0, R3.Pin_1, Part1.A0
  N2: R2.pin_0, R4.Pin_1, Part1.A2
  N3: R2.pin_1, Part1.RAW
  N4: R3.Pin_0, R4.Pin_0, S1.Pin_3, S1.Pin_4, Part1.GND
  N5: S1.Pin_1, S1.Pin_2, Part1.D2
